# Fritzing sketch Nenita_neu (saved by Fritzing 0.9.3b)
breadboards: 1

parts:
  Bauteil1 = Arduino Uno (Rev3)
  J1 = Basic Servo
  J2 = Basic Servo
  Bauteil2 = Arduino Uno (Rev3) - ICSP
  Bauteil3 = Arduino Uno (Rev3) - ICSP  # not connected

nets:
  N1: Bauteil1.D9_PWM, J1.pulse
  5V: Bauteil1.5V, J1.vcc
  GND: Bauteil1.GND, J1.gnd
  GND_2: J2.gnd, Bauteil2.GND
  VCC: J2.vcc, Bauteil2.5V
  N2: J2.pulse, Bauteil2.D9_PWM

// code stored in the sketch: nenita_neu.ino
#include <Servo.h>

Servo servoA;
int angle = 0;

void setup() {

servoA.attach(9);
servoA.write(30);

}
void loop() {

 for(int angle = 30;angle < 180; angle++)
   {
     servoA.write(angle);
     delay(15);
   }
   for(int angle = 180;angle > 30; angle--)
{
servoA.write(angle);
delay(15);
}
}
